// Logisim project p2orga1.circ as structural Verilog: 5 circuits, main circuit main
module main (
  input  in_1,
  input  in_2,
  output out_3
);

  nor nor_1 (out_3, in_1, in_2);
endmodule

module p2ej4c (
  input  A,
  input  B,
  input  C,
  input  D,
  output out_5
);

  wire and_1_out, and_2_out, and_3_out, and_4_out, and_5_out, and_6_out, not_1_out, not_2_out, not_3_out,
       not_4_out, not_5_out, or_1_out, or_2_out, or_3_out, or_4_out, or_5_out;

  not not_1 (not_1_out, A);
  not not_2 (not_2_out, B);
  not not_3 (not_3_out, C);
  not not_4 (not_4_out, D);
  not not_5 (not_5_out, D);
  and and_1 (and_1_out, not_1_out, not_2_out);
  and and_2 (and_2_out, not_3_out, not_4_out);
  or or_1 (or_1_out, A, B);
  or or_2 (or_2_out, C, D);
  and and_3 (and_3_out, A, B);
  and and_4 (and_4_out, B, not_5_out);
  and and_5 (and_5_out, and_1_out, and_2_out);
  and and_6 (and_6_out, or_1_out, or_2_out);
  or or_3 (or_3_out, and_3_out, C);
  or or_4 (or_4_out, and_5_out, and_6_out);
  or or_5 (or_5_out, or_3_out, and_4_out);
  and and_7 (out_5, or_4_out, or_5_out);
endmodule

module p2ej5a (
  input  A,
  input  B,
  input  C,
  output out_4
);

  wire and_1_out, and_2_out, and_3_out, and_4_out, and_5_out, and_6_out, and_7_out, and_8_out, not_1_out,
       not_2_out, not_3_out, not_4_out, or_1_out, or_2_out;

  not not_1 (not_1_out, B);
  not not_2 (not_2_out, C);
  not not_3 (not_3_out, B);
  not not_4 (not_4_out, A);
  and and_1 (and_1_out, A, not_1_out);
  and and_2 (and_2_out, A, not_3_out);
  and and_3 (and_3_out, not_4_out, B);
  and and_4 (and_4_out, A, B);
  and and_5 (and_5_out, and_2_out, C);
  and and_6 (and_6_out, and_3_out, C);
  and and_7 (and_7_out, and_4_out, C);
  and and_8 (and_8_out, and_1_out, not_2_out);
  or or_1 (or_1_out, and_8_out, and_5_out);
  or or_2 (or_2_out, and_6_out, and_7_out);
  or or_3 (out_4, or_1_out, or_2_out);
endmodule

module p2ej5fsimplificado (
  input  A,
  input  B,
  input  C,
  output out_4
);

  wire and_1_out, and_2_out, nor_1_out, or_1_out;

  nor nor_1 (nor_1_out, B, C);
  or or_1 (or_1_out, A, B);
  and and_1 (and_1_out, A, nor_1_out);
  and and_2 (and_2_out, C, or_1_out);
  or or_2 (out_4, and_1_out, and_2_out);
endmodule

module p2ej5bGsimplificado (
  input  D,
  input  E,
  input  F,
  output out_4
);

  wire and_1_out, and_2_out, not_1_out, not_2_out, not_3_out, or_1_out, or_2_out;

  not not_1 (not_1_out, E);
  not not_2 (not_2_out, F);
  not not_3 (not_3_out, D);
  or or_1 (or_1_out, D, not_1_out);
  or or_2 (or_2_out, not_3_out, E);
  and and_1 (and_1_out, or_1_out, not_2_out);
  and and_2 (and_2_out, F, or_2_out);
  or or_3 (out_4, and_1_out, and_2_out);
endmodule
